// Logisim project guia_2.circ as structural Verilog
module deMultiplexor (
  input  c1,
  input  c0,
  input  e0,
  output s0,
  output s1,
  output s2,
  output s3
);

  and and_1 (s0, ~c1, e0, ~c0);  // AND_Gate
  and and_2 (s1, ~c1, e0, c0);  // AND_Gate
  and and_3 (s2, c1, e0, ~c0);  // AND_Gate
  and and_4 (s3, c1, e0, c0);
endmodule

module inversor (
  input  e2,
  input  e1,
  input  e0,
  input  c0,
  output s2,
  output s1,
  output s0
);

  xor xor_1 (s2, c0, e2);
  xor xor_2 (s1, c0, e1);
  xor xor_3 (s0, c0, e0);
endmodule

module inversoAditivo (
  input  e0,
  input  e1,
  input  e2,
  input  e3,
  output s0,
  output s1,
  output s2,
  output s3
);
endmodule

module sumBin4b (
  input  m3,
  input  m2,
  input  m1,
  input  m0,
  input  n0,
  input  n1,
  input  n2,
  input  n3
);

  wire sumbin1b_2_co, sumbin1b_3_co, sumbin1b_4_co;

  sumBin1b sumbin1b_1 (.e1(n3), .e0(m3), .cI(sumbin1b_2_co));  // open: cO, res
  sumBin1b sumbin1b_2 (.cO(sumbin1b_2_co), .e1(n2), .e0(m2), .cI(sumbin1b_3_co));  // open: res
  sumBin1b sumbin1b_3 (.cO(sumbin1b_3_co), .e1(n1), .e0(m1), .cI(sumbin1b_4_co));  // open: res
  sumBin1b sumbin1b_4 (.cO(sumbin1b_4_co), .e1(n0), .e0(m0));  // open: res, cI
endmodule

module sumBin1b (
  input  e1,
  input  e0,
  input  cI,
  output cO,
  output res
);

  wire and_1_out, and_2_out, xor_1_out;

  or or_1 (cO, and_1_out, and_2_out);
  and and_1 (and_1_out, e0, e1);
  and and_2 (and_2_out, cI, xor_1_out);
  xor xor_1 (xor_1_out, e1, e0);
  xor xor_2 (res, xor_1_out, cI);
endmodule
